// Logisim project traffic_controller.circ as structural Verilog: 8 circuits, main circuit traffic_controller
module main (
  output R1r,
  output R1y,
  output R1g,
  output R2r,
  output R4r,
  output R4y,
  output R2y,
  output R2g,
  output R4g,
  output R3r,
  output R3y,
  output R3g
);

  wire ALU_zero_bit, and_1_out, clock_1_out, Control_Unit_asrc, Control_Unit_brn, Control_Unit_m2r,
       Control_Unit_mr, Control_Unit_mw, Control_Unit_rdst, or_1_out, Reg_File_p5;
  wire [1:0] Control_Unit_alu_op;
  wire [2:0] alu_cont_1_out_3;
  wire [4:0] multiplexer_4_out, splitter_reg_1_rd, splitter_reg_1_rs, splitter_reg_1_rt;
  wire [5:0] splitter_reg_1_fnctn, splitter_reg_1_opcode;
  wire [15:0] splitter_reg_1_imm;
  wire [23:0] shifter_1_out, shifter_3_out, splttr_2_out_2, splttr_out_2;
  wire [28:0] multiplexer_3_out;
  wire [28:28] rom_1_data_2;
  wire [30:0] rom_1_data;
  wire [31:0] adder_1_out, adder_2_out, ALU_alu_output, bit_extender_1_out, multiplexer_1_out,
       multiplexer_2_out, multiplexer_5_out, ram_1_data, Reg_File_p4, Reg_File_p6, Reg_File_p7, register_1_q,
       shifter_2_out;

  Clock clock_1 (.out(clock_1_out));
  Adder #(.width(32)) adder_1 (.a(register_1_q), .b(32'h4), .out(adder_1_out));  // open: cin, cout
  Register #(.width(32)) register_1 (.D(multiplexer_1_out), .Q(register_1_q), .clk(clock_1_out));  // open: en, clr
  Splitter_for_Mems splttr (.in_1(register_1_q), .out_2(splttr_out_2));
  Shifter #(.width(24), .shift("lr")) shifter_1 (.in(splttr_out_2), .\dist (5'b00010), .out(shifter_1_out));
  Multiplexer #(.width(32), .enable("false")) multiplexer_1 (
    .in0(adder_1_out), .in1(adder_2_out), .out(multiplexer_1_out), .sel(and_1_out));
  Multiplexer #(.width(32), .enable("false")) multiplexer_2 (
    .in0({rom_1_data[30:28], rom_1_data_2[28], rom_1_data[27:0]}), .in1(32'h1000fff7),
    .out(multiplexer_2_out), .sel(rom_1_data_2[28]));
  Splitter_Reg splitter_reg_1 (
    .in_1(multiplexer_2_out), .fnctn(splitter_reg_1_fnctn), .OpCode(splitter_reg_1_opcode),
    .rs(splitter_reg_1_rs), .rt(splitter_reg_1_rt), .rd(splitter_reg_1_rd), .imm(splitter_reg_1_imm));  // open: out_2
  ROM #(.addrWidth(24), .dataWidth(32)) rom_1 (
    .addr(shifter_1_out), .data({rom_1_data[30:28], rom_1_data_2[28], rom_1_data[27:0]}));  // open: sel
  Multiplexer #(.width(32), .enable("false")) multiplexer_3 (
    .in0({rom_1_data[30:28], rom_1_data_2[28], rom_1_data[27:0]}), .in1(32'h2442),
    .out({multiplexer_3_out[28:12], R1r, R1y, R1g, multiplexer_3_out[8], R2r, R2y, R2g, multiplexer_3_out[4], R3r, R3y, R3g, multiplexer_3_out[0], R4r, R4y, R4g}),
    .sel(rom_1_data_2[28]));
  Multiplexer #(.width(5), .enable("false")) multiplexer_4 (
    .in0(splitter_reg_1_rt), .in1(splitter_reg_1_rd), .out(multiplexer_4_out), .sel(Control_Unit_rdst));
  assign bit_extender_1_out = {{16{splitter_reg_1_imm[15]}}, splitter_reg_1_imm};  // Bit_Extender bit_extender_1
  and and_1 (and_1_out, Control_Unit_brn, ALU_zero_bit);
  // _32_register_file Reg_File: pin names not known; wires that end beside it: splitter_reg_1_rs, splitter_reg_1_rt, multiplexer_4_out, Reg_File_p4, Reg_File_p5, Reg_File_p6, Reg_File_p7
  Control_Unit Control_Unit (
    .in_1(splitter_reg_1_opcode), .RDST(Control_Unit_rdst), .RW(Reg_File_p5), .ASRC(Control_Unit_asrc),
    .MW(Control_Unit_mw), .MR(Control_Unit_mr), .M2R(Control_Unit_m2r), .BRN(Control_Unit_brn),
    .ALU_op(Control_Unit_alu_op));  // open: JMP
  Shifter #(.width(32)) shifter_2 (.in(bit_extender_1_out), .\dist (5'b00010), .out(shifter_2_out));
  Multiplexer #(.width(32), .enable("false")) multiplexer_5 (
    .in0(Reg_File_p7), .in1(bit_extender_1_out), .out(multiplexer_5_out), .sel(Control_Unit_asrc));
  ALU_Cont alu_cont_1 (.OPC(Control_Unit_alu_op), .FUN(splitter_reg_1_fnctn), .out_3(alu_cont_1_out_3));
  Adder #(.width(32)) adder_2 (.a(adder_1_out), .b(shifter_2_out), .out(adder_2_out));  // open: cin, cout
  ALU_main ALU (
    .A(Reg_File_p6), .B(multiplexer_5_out), .S0S1S2(alu_cont_1_out_3), .Zero_Bit(ALU_zero_bit),
    .Alu_Output(ALU_alu_output));
  Splitter_for_Mems splttr_2 (.in_1(ALU_alu_output), .out_2(splttr_2_out_2));
  Shifter #(.width(24), .shift("lr")) shifter_3 (.in(splttr_2_out_2), .\dist (5'b00010), .out(shifter_3_out));
  or or_1 (or_1_out, Control_Unit_mw, Control_Unit_mr);
  RAM #(.addrWidth(24), .dataWidth(32), .bus("separate")) ram_1 (
    .addr(shifter_3_out), .din(Reg_File_p7), .data(ram_1_data), .str(Control_Unit_mw), .sel(or_1_out),
    .clk(clock_1_out), .ld(Control_Unit_mr));  // open: clr
  Multiplexer #(.width(32), .enable("false")) multiplexer_6 (
    .in0(ram_1_data), .in1(ALU_alu_output), .out(Reg_File_p4), .sel(Control_Unit_m2r));

  // Notes on the sheet:
  //   contents of rom_1 (hex, n*v repeats v):
  //   0 7777 0 7777 0 7777 0 1444 2244 4144 4224 4414 4422 4441 2442 1000fff7
endmodule

module Splitter_Reg (
  input  [31:0] in_1,
  output [25:0] out_2,
  output [4:0] rs,
  output [4:0] rt,
  output [4:0] rd,
  output [5:0] OpCode,
  output [5:0] fnctn,
  output [15:0] imm
);


  assign fnctn = in_1[5:0];
  assign imm = in_1[15:0];
  assign OpCode = in_1[31:26];
  assign out_2 = in_1[25:0];
  assign rd = in_1[15:11];
  assign rs = in_1[25:21];
  assign rt = in_1[20:16];
endmodule

module Spliier_PC (
  input  [31:0] in_1,
  output [3:0] out_2
);


  assign out_2 = in_1[31:28];
endmodule

module Join_PC (
  input  [27:0] in_1,
  input  [3:0] in_2,
  output [31:0] out_3
);


  assign out_3 = {in_2, in_1};
endmodule

module Splitter_for_Mems (
  input  [31:0] in_1,
  output [23:0] out_2
);


  assign out_2 = in_1[23:0];
endmodule

module Control_Unit (
  input  [5:0] in_1,
  output RDST,
  output RW,
  output ASRC,
  output MW,
  output MR,
  output M2R,
  output BRN,
  output JMP,
  output [1:0] ALU_op
);

  wire and_3_out, and_4_out, not_1_out, not_2_out, not_3_out, not_4_out, not_5_out, not_6_out, not_7_out,
       not_8_out, not_9_out, not_10_out;

  not not_1 (not_1_out, in_1[3]);
  not not_2 (not_2_out, in_1[1]);
  not not_3 (not_3_out, in_1[2]);
  not not_4 (not_4_out, in_1[1]);
  not not_5 (not_5_out, in_1[3]);
  or or_1 (ASRC, in_1[1], in_1[3]);
  and and_1 (MW, in_1[5], in_1[3]);
  not not_6 (not_6_out, in_1[3]);
  not not_7 (not_7_out, in_1[0]);
  not not_8 (not_8_out, in_1[3]);
  not not_9 (not_9_out, in_1[2]);
  not not_10 (not_10_out, in_1[1]);
  and and_2 (RDST, not_1_out, not_2_out);
  and and_3 (and_3_out, not_3_out, not_4_out);
  or or_2 (RW, and_3_out, and_4_out);
  and and_4 (and_4_out, in_1[5], not_5_out);
  and and_5 (MR, in_1[5], not_6_out);
  and and_6 (JMP, in_1[1], not_7_out);
  and and_7 (ALU_op[1], not_8_out, not_9_out, not_10_out);

  assign ALU_op[0] = in_1[2];
  assign BRN = in_1[2];
  assign M2R = in_1[1];
endmodule

module ALU_Cont (
  input  [1:0] OPC,
  input  [5:0] FUN,
  output [2:0] out_3
);

  wire and_1_out, and_2_out, and_3_out, and_4_out, not_1_out, not_2_out, not_3_out;

  not not_1 (not_1_out, FUN[5]);
  not not_2 (not_2_out, OPC[1]);
  not not_3 (not_3_out, FUN[2]);
  and and_1 (and_1_out, OPC[1], FUN[0]);
  and and_2 (and_2_out, OPC[1], FUN[3]);
  and and_3 (and_3_out, OPC[1], not_1_out);
  and and_4 (and_4_out, OPC[1], FUN[1]);
  or or_1 (out_3[1], not_2_out, not_3_out);
  or or_2 (out_3[0], and_1_out, and_2_out);
  or or_3 (out_3[2], OPC[0], and_3_out, and_4_out);
endmodule

module traffic_controller (
);

  wire main_1_r1g, main_1_r1r, main_1_r1y, main_1_r2g, main_1_r2r, main_1_r2y, main_1_r3g, main_1_r3r,
       main_1_r3y, main_1_r4g, main_1_r4r, main_1_r4y;

  LED led_1 (.in(main_1_r4r));
  LED led_2 (.in(main_1_r4y));
  LED led_3 (.in(main_1_r4g));
  LED led_4 (.in(main_1_r1y));
  LED led_5 (.in(main_1_r1r));
  LED led_6 (.in(main_1_r1g));
  main main_1 (
    .R4r(main_1_r4r), .R4y(main_1_r4y), .R4g(main_1_r4g), .R1r(main_1_r1r), .R1y(main_1_r1y),
    .R1g(main_1_r1g), .R3r(main_1_r3r), .R3y(main_1_r3y), .R3g(main_1_r3g), .R2r(main_1_r2r),
    .R2y(main_1_r2y), .R2g(main_1_r2g));
  LED led_7 (.in(main_1_r3g));
  LED led_8 (.in(main_1_r3y));
  LED led_9 (.in(main_1_r3r));
  LED led_10 (.in(main_1_r2r));
  LED led_11 (.in(main_1_r2y));
  LED led_12 (.in(main_1_r2g));

  // Notes on the sheet:
  //   ROAD 4
  //   ROAD 1
  //   ROAD 3
  //   ROAD 2
endmodule
